# Fritzing sketch CSAWSchematic2 (saved by Fritzing 0.9.3b)
breadboards: 3

parts:
  U1 = 74HC4051 [package=so16]
  U2 = 74HC4051 [package=so16]
  U3 = 74HC4051 [package=so16]
  U4 = 74HC4051 [package=so16]
  U5 = 74HC4051 [package=so16]
  U6 = 74HC4051 [package=so16]
  U7 = 74HC4051 [package=so16]
  U8 = 74HC4051 [package=so16]
  CSAW = Arduino Mega 2560 (Rev3)
  R1 = Rotary Potentiometer (Large) [maximum_resistance=10kΩ package=THT]
  R2 = Slide Potentiometer [maximum_resistance=10kΩ]
  R3 = Rotary Potentiometer (Large) [maximum_resistance=10kΩ package=THT]
  R4 = Rotary Potentiometer (Large) [maximum_resistance=10kΩ package=THT]
  R5 = Rotary Potentiometer (Large) [maximum_resistance=10kΩ package=THT]
  R6 = Rotary Potentiometer (Large) [maximum_resistance=10kΩ package=THT]
  R7 = Rotary Potentiometer (Large) [maximum_resistance=10kΩ package=THT]
  R8 = Rotary Potentiometer (Large) [maximum_resistance=10kΩ package=THT]
  R9 = Rotary Potentiometer (Large) [maximum_resistance=10kΩ package=THT]
  R10 = Rotary Potentiometer (Large) [maximum_resistance=10kΩ package=THT]
  R11 = Rotary Potentiometer (Large) [maximum_resistance=10kΩ package=THT]
  R12 = Rotary Potentiometer (Large) [maximum_resistance=10kΩ package=THT]
  R13 = Rotary Potentiometer (Large) [maximum_resistance=10kΩ package=THT]
  R14 = Slide Potentiometer [maximum_resistance=10kΩ]
  R15 = Rotary Potentiometer (Large) [maximum_resistance=10kΩ package=THT]
  R16 = Rotary Potentiometer (Large) [maximum_resistance=10kΩ package=THT]
  R17 = Rotary Potentiometer (Large) [maximum_resistance=10kΩ package=THT]
  R18 = Rotary Potentiometer (Large) [maximum_resistance=10kΩ package=THT]
  R19 = Rotary Potentiometer (Large) [maximum_resistance=10kΩ package=THT]
  R20 = Rotary Potentiometer (Large) [maximum_resistance=10kΩ package=THT]
  R21 = Rotary Potentiometer (Large) [maximum_resistance=10kΩ package=THT]
  R22 = Rotary Potentiometer (Large) [maximum_resistance=10kΩ package=THT]
  R23 = Rotary Potentiometer (Large) [maximum_resistance=10kΩ package=THT]
  R24 = Rotary Potentiometer (Large) [maximum_resistance=10kΩ package=THT]
  R25 = Rotary Potentiometer (Large) [maximum_resistance=10kΩ package=THT]
  R26 = Rotary Potentiometer (Large) [maximum_resistance=10kΩ package=THT]
  R27 = Slide Potentiometer [maximum_resistance=10kΩ]
  R28 = Slide Potentiometer [maximum_resistance=10kΩ]
  R29 = Rotary Potentiometer (Large) [maximum_resistance=10kΩ package=THT]
  R30 = Rotary Potentiometer (Large) [maximum_resistance=10kΩ package=THT]
  R31 = Rotary Potentiometer (Large) [maximum_resistance=10kΩ package=THT]
  R32 = Rotary Potentiometer (Large) [maximum_resistance=10kΩ package=THT]
  R33 = Rotary Potentiometer (Large) [maximum_resistance=10kΩ package=THT]
  R34 = Slide Potentiometer [maximum_resistance=10kΩ]
  R35 = Rotary Potentiometer (Large) [maximum_resistance=10kΩ package=THT]
  R36 = Rotary Potentiometer (Large) [maximum_resistance=10kΩ package=THT]
  R37 = Rotary Potentiometer (Large) [maximum_resistance=10kΩ package=THT]
  R38 = Rotary Potentiometer (Large) [maximum_resistance=10kΩ package=THT]
  R39 = Rotary Potentiometer (Large) [maximum_resistance=10kΩ package=THT]
  R40 = Slide Potentiometer [maximum_resistance=10kΩ]
  R41 = Rotary Potentiometer (Large) [maximum_resistance=10kΩ package=THT]
  R42 = Rotary Potentiometer (Large) [maximum_resistance=10kΩ package=THT]
  R43 = Rotary Potentiometer (Large) [maximum_resistance=10kΩ package=THT]
  R44 = Rotary Potentiometer (Large) [maximum_resistance=10kΩ package=THT]
  R45 = Rotary Potentiometer (Large) [maximum_resistance=10kΩ package=THT]
  R46 = Slide Potentiometer [maximum_resistance=10kΩ]
  R47 = Rotary Potentiometer (Large) [maximum_resistance=10kΩ package=THT]
  R48 = Rotary Potentiometer (Large) [maximum_resistance=10kΩ package=THT]
  R49 = Rotary Potentiometer (Large) [maximum_resistance=10kΩ package=THT]
  R50 = Rotary Potentiometer (Large) [maximum_resistance=10kΩ package=THT]
  R51 = Rotary Potentiometer (Large) [maximum_resistance=10kΩ package=THT]
  R52 = Slide Potentiometer [maximum_resistance=10kΩ]
  S1 = Pushbutton [package="[SMD]"]
  R53 = Resistor [tolerance=±5% resistance=10k package="2010 [SMD]"]
  S2 = Pushbutton [package="[SMD]"]
  R54 = Resistor [tolerance=±5% resistance=10k package="2010 [SMD]"]
  S3 = Pushbutton [package="[SMD]"]
  S4 = Pushbutton [package="[SMD]"]
  R55 = Resistor [tolerance=±5% resistance=10k package="2010 [SMD]"]
  R56 = Resistor [tolerance=±5% resistance=10k package="2010 [SMD]"]
  S5 = Pushbutton [package="[SMD]"]
  S6 = Pushbutton [package="[SMD]"]
  S7 = Pushbutton [package="[SMD]"]
  S8 = Pushbutton [package="[SMD]"]
  R57 = Resistor [tolerance=±5% resistance=10k package="2010 [SMD]"]
  R58 = Resistor [tolerance=±5% resistance=10k package="2010 [SMD]"]
  R59 = Resistor [tolerance=±5% resistance=10k package="2010 [SMD]"]
  R60 = Resistor [tolerance=±5% resistance=10k package="2010 [SMD]"]
  S9 = Pushbutton [package="[SMD]"]
  S11 = Pushbutton [package="[SMD]"]
  S10 = Pushbutton [package="[SMD]"]
  R61 = Resistor [tolerance=±5% resistance=10k package="2010 [SMD]"]
  R62 = Resistor [tolerance=±5% resistance=10k package="2010 [SMD]"]
  R64 = Resistor [tolerance=±5% resistance=10k package="2010 [SMD]"]
  R65 = Slide Potentiometer [maximum_resistance=10kΩ]
  R66 = Slide Potentiometer [maximum_resistance=10kΩ]
  Part1 = SparkFun ESP8266 Thing

nets:
  N1: U1.IO4, R5.wiper
  N2: U1.IO6, R7.wiper
  N3: U1.IO, CSAW.A0
  N4: U1.IO5, R6.wiper
  VSS: U1.INH, U1.VEE, U1.VSS, U2.INH, U2.VEE, U2.VSS, U3.INH, U3.VEE, U3.VSS, U4.INH, U4.VEE, U4.VSS, CSAW.GND, R1.leg2, R2.leg2, R3.leg2, R4.leg2, R5.leg2, R6.leg2, R7.leg2, R8.leg2, R9.leg2, R10.leg2, R11.leg2, R12.leg2, R13.leg2, R14.leg2, R15.leg2, R16.leg2, R17.leg2, R18.leg2, R19.leg2, R20.leg2, R21.leg2, R22.leg2, R23.leg2, R24.leg2, R25.leg2, R26.leg2, R27.leg2, R28.leg2, R48.leg2, R49.leg2, R50.leg2, R52.leg2, R53.Pin_1, R54.Pin_1, R55.Pin_1, R56.Pin_1, R57.Pin_1, R58.Pin_1, R59.Pin_1, R60.Pin_1, R61.Pin_1, R62.Pin_1, R64.Pin_1, R65.leg2, R66.leg2, Part1.GND
  N5: U1.C, CSAW.D4_PWM
  N6: U1.B, CSAW.D3_PWM
  N7: U1.A, CSAW.D2_PWM
  N8: U1.IO3, R4.wiper
  N9: U1.IO0, R2.wiper
  N10: U1.IO1, R1.wiper
  N11: U1.IO2, R3.wiper
  VDD: U1.VDD, U2.VDD, U3.VDD, U4.VDD, U5.VDD, U6.VDD, U7.VDD, U8.VDD, CSAW.5V, R1.leg1, R2.leg1, R3.leg1, R4.leg1, R5.leg1, R6.leg1, R7.leg1, R8.leg1, R9.leg1, R10.leg1, R11.leg1, R12.leg1, R13.leg1, R14.leg1, R15.leg1, R16.leg1, R17.leg1, R18.leg1, R19.leg1, R20.leg1, R21.leg1, R22.leg1, R23.leg1, R24.leg1, R25.leg1, R26.leg1, R27.leg1, R28.leg1, R48.leg1, R49.leg1, R50.leg1, R52.leg1, S1.Pin_3, S1.Pin_4, S2.Pin_3, S2.Pin_4, S3.Pin_3, S3.Pin_4, S4.Pin_4, S5.Pin_3, S5.Pin_4, S6.Pin_3, S6.Pin_4, S7.Pin_3, S7.Pin_4, S8.Pin_4, S9.Pin_3, S9.Pin_4, S11.Pin_3, S11.Pin_4, S10.Pin_3, S10.Pin_4, R65.leg1, R66.leg1, Part1.VIN
  N12: U2.IO4, R9.wiper
  N13: U2.IO6, R13.wiper
  N14: U2.IO, CSAW.A1
  N15: U2.IO5, R10.wiper
  N16: U2.C, CSAW.D7_PWM
  N17: U2.B, CSAW.D6_PWM
  N18: U2.A, CSAW.D5_PWM
  N19: U2.IO3, R12.wiper
  N20: U2.IO0, R14.wiper
  N21: U2.IO1, R8.wiper
  N22: U2.IO2, R11.wiper
  N23: U3.IO4, R24.wiper
  N24: U3.IO6, R18.wiper
  N25: U3.IO, CSAW.A3
  N26: U3.IO5, R20.wiper
  N27: U3.C, CSAW.D13_PWM
  N28: U3.B, CSAW.D12_PWM
  N29: U3.A, CSAW.D11_PWM
  N30: U3.IO3, R25.wiper
  N31: U3.IO0, R28.wiper
  N32: U3.IO1, R22.wiper
  N33: U3.IO2, R21.wiper
  N34: U4.IO4, R19.wiper
  N35: U4.IO6, R26.wiper
  N36: U4.IO, CSAW.A2
  N37: U4.IO5, R16.wiper
  N38: U4.C, CSAW.D10_PWM
  N39: U4.B, CSAW.D9_PWM
  N40: U4.A, CSAW.D8_PWM
  N41: U4.IO3, R17.wiper
  N42: U4.IO0, R27.wiper
  N43: U4.IO1, R15.wiper
  N44: U4.IO2, R23.wiper
  N45: U5.IO4, R35.wiper
  N46: U5.IO, CSAW.A5
  N47: U5.IO5, R39.wiper
  VSS_2: U5.INH, U5.VEE, U5.VSS, U6.INH, U6.VEE, U6.VSS, U7.INH, U7.VEE, U7.VSS, U8.INH, U8.VEE, U8.VSS, R29.leg2, R30.leg2, R31.leg2, R32.leg2, R33.leg2, R34.leg2, R35.leg2, R36.leg2, R37.leg2, R38.leg2, R39.leg2, R40.leg2, R41.leg2, R42.leg2, R43.leg2, R44.leg2, R45.leg2, R46.leg2, R47.leg2, R51.leg2
  N48: U5.C, CSAW.D28
  N49: U5.B, CSAW.D27
  N50: U5.A, CSAW.D26
  N51: U5.IO3, R36.wiper
  N52: U5.IO0, R40.wiper
  N53: U5.IO1, R37.wiper
  N54: U5.IO2, R38.wiper
  N55: U6.IO4, R33.wiper
  N56: U6.IO, CSAW.A4
  N57: U6.IO5, R32.wiper
  N58: U6.C, CSAW.D24
  N59: U6.B, CSAW.D23
  N60: U6.A, CSAW.D22
  N61: U6.IO3, R29.wiper
  N62: U6.IO0, R34.wiper
  N63: U6.IO1, R31.wiper
  N64: U6.IO2, R30.wiper
  N65: U7.IO4, R47.wiper
  N66: U7.IO, CSAW.A7
  N67: U7.IO5, R51.wiper
  N68: U7.C, CSAW.D36
  N69: U7.B, CSAW.D35
  N70: U7.A, CSAW.D34
  N71: U7.IO3, R48.wiper
  N72: U7.IO0, R52.wiper
  N73: U7.IO1, R49.wiper
  N74: U7.IO2, R50.wiper
  N75: U8.IO4, R41.wiper
  N76: U8.IO, CSAW.A6
  N77: U8.IO5, R45.wiper
  N78: U8.C, CSAW.D32
  N79: U8.B, CSAW.D31
  N80: U8.A, CSAW.D30
  N81: U8.IO3, R42.wiper
  N82: U8.IO0, R46.wiper
  N83: U8.IO1, R43.wiper
  N84: U8.IO2, R44.wiper
  N85: CSAW.A8, R65.wiper
  N86: CSAW.A9, R66.wiper
  N87: CSAW.D0_RX0, Part1.U0TXO
  N88: CSAW.D1_TX0, Part1.U0RXI
  N89: CSAW.D41, S1.Pin_1, S1.Pin_2
  N90: CSAW.D42, S2.Pin_1, S2.Pin_2
  N91: CSAW.D43, S3.Pin_1, S3.Pin_2
  N92: CSAW.D44, S4.Pin_1, S4.Pin_2
  N93: CSAW.D45, S5.Pin_1, S5.Pin_2
  N94: CSAW.D46, S8.Pin_1, S8.Pin_2
  N95: CSAW.D47, S7.Pin_1, S7.Pin_2
  N96: CSAW.D48, S6.Pin_1, S6.Pin_2
  N97: CSAW.D50, S9.Pin_1, S9.Pin_2
  N98: CSAW.D51, S10.Pin_1, S10.Pin_2
  N99: CSAW.D52, S11.Pin_1, S11.Pin_2
  N100: R29.leg1, R30.leg1, R31.leg1, R32.leg1, R33.leg1, R34.leg1, R35.leg1, R36.leg1, R37.leg1, R38.leg1, R39.leg1, R40.leg1, R41.leg1, R42.leg1, R43.leg1, R44.leg1, R45.leg1, R46.leg1, R47.leg1, R51.leg1
